// Logisim project Arithmetic.circ as structural Verilog: 1 circuit, main circuit Adder
module Adder (
  input  A,
  input  B,
  input  c_in,
  output S,
  output c_out
);

  wire and_1_q, and_2_q, and_3_q, and_4_q, not_1_q, not_2_q, or_1_q, xor_1_q;

  AND_Gate and_1 (.A(A), .B(B), .Q(and_1_q));
  NOT_Gate not_1 (.A(A), .Q(not_1_q));
  AND_Gate and_2 (.A(not_1_q), .B(B), .Q(and_2_q));
  AND_Gate and_3 (.A(A), .B(not_2_q), .Q(and_3_q));
  NOT_Gate not_2 (.A(B), .Q(not_2_q));
  XOR_Gate xor_1 (.A(A), .B(B), .Q(xor_1_q));
  AND_Gate and_4 (.A(c_in), .B(or_1_q), .Q(and_4_q));
  OR_Gate or_1 (.A(and_2_q), .B(and_3_q), .Q(or_1_q));
  XOR_Gate xor_2 (.A(xor_1_q), .B(c_in), .Q(S));
  OR_Gate or_2 (.A(and_1_q), .B(and_4_q), .Q(c_out));

  // Notes on the sheet:
  //   Full Bit Adder
endmodule
