// Logisim project Gates.circ as structural Verilog: 6 circuits, main circuit NOT Gate
module NOT_Gate (
  input  A,
  output Q
);

  Transistor transistor_1 (.in(1'b1), .out(Q), .gate(A));
  Transistor #(.\type ("n")) transistor_2 (.in(1'b0), .out(Q), .gate(A));

  // Notes on the sheet:
  //   NOT Gate
endmodule

module NAND_Gate (
  input  A,
  input  B,
  output Q
);

  wire transistor_3_out;

  Transistor transistor_1 (.in(1'b1), .out(Q), .gate(A));
  Transistor #(.\type ("n")) transistor_2 (.in(transistor_3_out), .out(Q), .gate(A));
  Transistor #(.\type ("n")) transistor_3 (.in(1'b0), .out(transistor_3_out), .gate(B));
  Transistor transistor_4 (.in(1'b1), .out(Q), .gate(B));

  // Notes on the sheet:
  //   NAND Gate
endmodule

module AND_Gate (
  input  A,
  input  B,
  output Q
);

  wire transistor_1_out, transistor_3_out;

  Transistor transistor_1 (.in(1'b1), .out(transistor_1_out), .gate(A));
  Transistor #(.\type ("n")) transistor_2 (.in(transistor_3_out), .out(transistor_1_out), .gate(A));
  Transistor #(.\type ("n")) transistor_3 (.in(1'b0), .out(transistor_3_out), .gate(B));
  Transistor transistor_4 (.in(1'b1), .out(transistor_1_out), .gate(B));
  Transistor transistor_5 (.in(1'b1), .out(Q), .gate(transistor_1_out));
  Transistor #(.\type ("n")) transistor_6 (.in(1'b0), .out(Q), .gate(transistor_1_out));

  // Notes on the sheet:
  //   AND Gate
endmodule

module NOR_Gate (
  input  A,
  input  B,
  output Q
);

  wire transistor_1_out;

  Transistor transistor_1 (.in(1'b1), .out(transistor_1_out), .gate(A));
  Transistor transistor_2 (.in(transistor_1_out), .out(Q), .gate(B));
  Transistor #(.\type ("n")) transistor_3 (.in(1'b0), .out(Q), .gate(B));
  Transistor #(.\type ("n")) transistor_4 (.in(1'b0), .out(Q), .gate(A));

  // Notes on the sheet:
  //   NOR Gate
endmodule

module OR_Gate (
  input  A,
  input  B,
  output Q
);

  wire transistor_1_out, transistor_2_out;

  Transistor transistor_1 (.in(1'b1), .out(transistor_1_out), .gate(A));
  Transistor transistor_2 (.in(transistor_1_out), .out(transistor_2_out), .gate(B));
  Transistor #(.\type ("n")) transistor_3 (.in(1'b0), .out(transistor_2_out), .gate(A));
  Transistor #(.\type ("n")) transistor_4 (.in(1'b0), .out(transistor_2_out), .gate(B));
  Transistor transistor_5 (.in(1'b1), .out(Q), .gate(transistor_2_out));
  Transistor #(.\type ("n")) transistor_6 (.in(1'b0), .out(Q), .gate(transistor_2_out));

  // Notes on the sheet:
  //   OR Gate
endmodule

module XOR_Gate (
  input  A,
  input  B,
  output Q
);

  wire NAND, OR, transistor_1_out, transistor_2_out, transistor_8_out, transistor_11_out, transistor_14_out;

  Transistor transistor_1 (.in(1'b1), .out(transistor_1_out), .gate(A));
  Transistor transistor_2 (.in(transistor_1_out), .out(transistor_2_out), .gate(B));
  Transistor #(.\type ("n")) transistor_3 (.in(1'b0), .out(transistor_2_out), .gate(A));
  Transistor #(.\type ("n")) transistor_4 (.in(1'b0), .out(transistor_2_out), .gate(B));
  Transistor transistor_5 (.in(1'b1), .out(NAND), .gate(B));
  Transistor transistor_6 (.in(1'b1), .out(NAND), .gate(A));
  Transistor #(.\type ("n")) transistor_7 (.in(transistor_8_out), .out(NAND), .gate(A));
  Transistor #(.\type ("n")) transistor_8 (.in(1'b0), .out(transistor_8_out), .gate(B));
  Transistor transistor_9 (.in(1'b1), .out(OR), .gate(transistor_2_out));
  Transistor #(.\type ("n")) transistor_10 (.in(1'b0), .out(OR), .gate(transistor_2_out));
  Transistor transistor_11 (.in(1'b1), .out(transistor_11_out), .gate(OR));
  Transistor transistor_12 (.in(1'b1), .out(transistor_11_out), .gate(NAND));
  Transistor #(.\type ("n")) transistor_13 (.in(transistor_14_out), .out(transistor_11_out), .gate(OR));
  Transistor #(.\type ("n")) transistor_14 (.in(1'b0), .out(transistor_14_out), .gate(NAND));
  Transistor transistor_15 (.in(1'b1), .out(Q), .gate(transistor_11_out));
  Transistor #(.\type ("n")) transistor_16 (.in(1'b0), .out(Q), .gate(transistor_11_out));

  // Notes on the sheet:
  //   XOR Gate
endmodule
