// Logisim project Plexers.circ as structural Verilog: 3 circuits, main circuit Multiplexer
module Multiplexer (
  input  Select,
  input  Input_1,
  input  Input_2,
  output Output
);

  wire and_1_q, and_2_q, not_1_q;

  NOT_Gate not_1 (.A(Select), .Q(not_1_q));
  AND_Gate and_1 (.A(not_1_q), .B(Input_1), .Q(and_1_q));
  OR_Gate or_1 (.A(and_1_q), .B(and_2_q), .Q(Output));
  AND_Gate and_2 (.A(Select), .B(Input_2), .Q(and_2_q));
endmodule

module Demultiplexer (
  input  Input,
  input  Select,
  output Output1,
  output Output2
);

  wire not_1_q;

  NOT_Gate not_1 (.A(Select), .Q(not_1_q));
  AND_Gate and_1 (.A(Input), .B(not_1_q), .Q(Output1));
  AND_Gate and_2 (.A(Input), .B(Select), .Q(Output2));
endmodule

module Priority_Encoder (
  input  Input1,
  input  Input2,
  input  Input3,
  input  Input4,
  output [1:0] out_5
);

  wire and_1_q, not_1_q;

  OR_Gate or_1 (.A(Input4), .B(Input3), .Q(out_5[1]));
  AND_Gate and_1 (.A(Input2), .B(not_1_q), .Q(and_1_q));
  NOT_Gate not_1 (.A(Input3), .Q(not_1_q));
  OR_Gate or_2 (.A(Input4), .B(and_1_q), .Q(out_5[0]));
endmodule
